# Fritzing sketch photocell (saved by Fritzing 0.9.9b)
breadboards: 1

parts:
  R1 = Resistor [tolerance=±5% power=0.25 resistance=300 package=THT]
  Power = Battery
  Vo = Multimeter straight red probe  # not connected
  part = Multimeter straight black probe
  R2 = Photocell (LDR) [package=THT]

nets:
  N1: R1.Pin_0, Power.+
  N2: R1.Pin_1, R2.pin_0
  GND: Power.-, part.Probe_meter_end, part.Probe_tip_2, R2.pin_1
