# Fritzing sketch smooth_LED (saved by Fritzing 0.9.9b)
breadboards: 1

parts:
  R1 = Resistor [tolerance=±5% power=0.25 resistance=220 package=THT]
  LED1 = LED - 5mm [color="Red (633nm)" current=0.030 package="5 mm [THT]"]
  Part1 = Arduino Uno (Rev3)
  R2 = Photocell (LDR) [package=THT]
  R3 = Resistor [tolerance=±5% power=0.25 resistance=10k package=THT]

nets:
  N1: R1.Pin_0, Part1.D3_PWM
  N2: R1.Pin_1, LED1.cathode
  N3: LED1.anode, Part1.GND
  N4: Part1.A0, R2.pin_0, R3.Pin_1
  N5: Part1.5V, R3.Pin_0
